# Fritzing sketch Untitled Sketch 2 (saved by Fritzing 0.9.3b)

parts:
  Componente1 = Arduino Micro (Rev3)
  Componente2 = Bluetooth HC-05 Macho

nets:
  GND: Componente1.GND, Componente2.GND
  N1: Componente1.D10_PWM/A10, Componente2.TXD
  N2: Componente1.D11_PWM, Componente2.RXD
  3V3: Componente1.3V3, Componente2.VCC
